// Logisim project simon_says_reduce_5_boxs.circ as structural Verilog: 6 circuits, main circuit main
// 3
module main (
);

  wire and_1_out, and_2_out, and_3_out, and_4_out, and_5_out, and_6_out, and_7_out, and_8_out, and_9_out,
       and_10_out, and_11_out, and_12_out, and_13_out, and_14_out, and_15_out, and_16_out, and_17_out,
       and_18_out, and_19_out, button_1_out, button_2_out, button_7_out, button_9_out, button_10_out,
       button_11_out, button_12_out, clock_1_out, clock_2_out, clock_3_out, clock_4_out, d_ff_1_q, d_ff_1_qn,
       d_ff_2_q, d_ff_2_qn, d_ff_3_q, d_ff_4_q, d_ff_4_qn, d_ff_5_q, d_ff_6_q, d_ff_7_q, d_ff_8_q, d_ff_8_qn,
       d_ff_9_q, d_ff_10_q, d_ff_11_q, demultiplexer_6_out0, demultiplexer_6_out5, dipswitch_1_p1,
       dipswitch_1_p2, dipswitch_1_p3, dipswitch_1_p4, dipswitch_2_p1, dipswitch_2_p2, dipswitch_2_p3,
       dipswitch_2_p4, multiplexer_1_out, multiplexer_2_out, multiplexer_3_out, multiplexer_4_out,
       multiplexer_5_out, multiplexer_6_out, multiplexer_7_out, multiplexer_8_out, multiplexer_9_out,
       multiplexer_10_out, n74175_1_pin1, n74175_1_pin2, n74175_1_pin4, n74175_1_pin5, n74175_1_pin7,
       n74175_1_pin9, n74175_1_pin10, n74175_1_pin12, n74175_1_pin13, n74175_1_pin15, n74175_2_pin2,
       n74175_2_pin4, n74175_2_pin5, n74175_2_pin7, n74175_2_pin9, n74175_2_pin10, n74175_2_pin12,
       n74175_2_pin13, n74175_2_pin15, n74175_3_pin2, n74175_3_pin4, n74175_3_pin5, n74175_3_pin7,
       n74175_3_pin9, n74175_3_pin10, n74175_3_pin12, n74175_3_pin13, n74175_3_pin15, n74175_4_pin2,
       n74175_4_pin4, n74175_4_pin5, n74175_4_pin7, n74175_4_pin9, n74175_4_pin10, n74175_4_pin12,
       n74175_4_pin13, n74175_4_pin15, n74175_5_pin2, n74175_5_pin4, n74175_5_pin5, n74175_5_pin7,
       n74175_5_pin9, n74175_5_pin10, n74175_5_pin12, n74175_5_pin13, n74175_5_pin15, nor_1_out, not_1_out,
       not_2_out, not_3_out, or_1_out, or_2_out, or_3_out, or_4_out, or_5_out, or_6_out, or_7_out, or_11_out,
       or_12_out, register_1_q, register_2_q, register_3_q, register_4_q, register_5_q, register_6_q,
       register_7_q, register_8_q, xnor_1_out, xnor_2_out, xnor_3_out, xnor_4_out, xnor_5_out, xnor_6_out,
       xnor_7_out;
  wire [0:0] or_10_out;
  wire [1:0] random_1_out;
  wire [2:0] counter_1_q, counter_3_q, counter_4_q, or_8_out, register_9_q;

  Clock clock_1 (.out(clock_1_out));
  Clock clock_2 (.out(clock_2_out));
  D_Flip_Flop d_ff_1 (.D(d_ff_1_qn), .clk(or_1_out), .Q(d_ff_1_q), .Qn(d_ff_1_qn), .reset(and_5_out));  // open: preset
  Register #(.width(1)) register_1 (.D(dipswitch_1_p1), .en(1'b1), .clk(clock_1_out), .Q(register_1_q), .clr(1'b0));
  Register #(.width(1)) register_2 (.D(dipswitch_2_p1), .en(1'b1), .clk(clock_2_out), .Q(register_2_q), .clr(1'b0));
  or or_1 (or_1_out, and_7_out, button_11_out);
  and and_1 (and_1_out, d_ff_5_q, clock_3_out);
  or or_2 (or_2_out, or_1_out, button_11_out);
  and and_2 (and_2_out, d_ff_1_q, and_1_out);
  and and_3 (and_3_out, and_2_out, d_ff_4_qn);
  D_Flip_Flop d_ff_2 (.D(1'b1), .clk(or_2_out), .Q(d_ff_2_q), .Qn(d_ff_2_qn), .reset(and_5_out));  // open: preset
  Clock clock_3 (.out(clock_3_out));
  // DipSwitch #(.number(4)) dipswitch_1: pin names not known; wires that end beside it: dipswitch_1_p1, dipswitch_1_p2, dipswitch_1_p3, dipswitch_1_p4
  // DipSwitch #(.number(4)) dipswitch_2: pin names not known; wires that end beside it: dipswitch_2_p1, dipswitch_2_p2, dipswitch_2_p3, dipswitch_2_p4
  or or_3 (or_3_out, or_1_out, and_2_out);
  D_Flip_Flop d_ff_3 (.D(1'b1), .clk(and_3_out), .Q(d_ff_3_q), .reset(and_5_out));  // open: Qn, preset
  Register #(.width(1)) register_3 (.D(dipswitch_1_p2), .en(1'b1), .clk(clock_1_out), .Q(register_3_q), .clr(1'b0));
  xnor xnor_1 (xnor_1_out, register_1_q, register_2_q);
  Register #(.width(1)) register_4 (.D(dipswitch_2_p2), .en(1'b1), .clk(clock_2_out), .Q(register_4_q), .clr(1'b0));
  and and_4 (and_4_out, not_1_out, and_7_out);
  not not_1 (not_1_out, or_10_out[0]);
  Counter #(.max('h7), .width(3)) counter_1 (
    .clr(and_5_out), .load(or_1_out), .count(1'b1), .clk(or_3_out), .Q(counter_1_q));  // open: up, D, carry
  D_Flip_Flop #(.trigger("falling")) d_ff_4 (
    .D(d_ff_3_q), .clk(and_3_out), .Q(d_ff_4_q), .Qn(d_ff_4_qn), .reset(and_5_out));  // open: preset
  D_Flip_Flop #(.trigger("falling")) d_ff_5 (
    .D(d_ff_2_q), .clk(clock_3_out), .Q(d_ff_5_q), .reset(and_5_out));  // open: Qn, preset
  Button button_1 (.out(button_1_out));
  Button button_2 (.out(button_2_out));
  xnor xnor_2 (xnor_2_out, register_3_q, register_4_q);
  Register #(.width(1)) register_5 (.D(dipswitch_2_p3), .en(1'b1), .clk(clock_2_out), .Q(register_5_q), .clr(1'b0));
  Counter counter_2 (
    .clr(button_1_out), .load(button_1_out), .count(button_2_out), .clk(button_2_out), .D(8'hf));  // open: up, carry, Q
  or or_4 (or_4_out, or_10_out[0], or_12_out);
  and and_5 (and_5_out, d_ff_4_q, not_2_out);
  not not_2 (not_2_out, or_11_out);
  Register #(.width(1)) register_6 (.D(dipswitch_1_p3), .en(1'b1), .clk(clock_1_out), .Q(register_6_q), .clr(1'b0));
  and and_6 (and_6_out, xnor_2_out, xnor_1_out);
  Counter #(.max('h7), .width(3)) counter_3 (
    .load(or_10_out[0]), .count(1'b1), .clk(or_4_out), .D({2'b00, or_10_out[0]}), .Q(counter_3_q));  // open: clr, up, carry
  and and_7 (and_7_out, xnor_4_out, xnor_5_out, xnor_7_out);
  D_Flip_Flop d_ff_6 (.D(and_11_out), .clk(d_ff_9_q), .Q(d_ff_6_q), .reset(or_5_out));  // open: Qn, preset
  Counter #(.max('h7), .width(3)) counter_4 (
    .clr(or_7_out), .up(1'b1), .count(1'b1), .clk(d_ff_6_q), .Q(counter_4_q));  // open: load, D, carry
  Button button_3 ();  // open: out
  Button button_4 ();  // open: out
  Button button_5 ();  // open: out
  D_Flip_Flop d_ff_7 (.D(1'b1), .clk(d_ff_11_q), .Q(d_ff_7_q), .reset(or_10_out[0]));  // open: Qn, preset
  and and_8 (and_8_out, d_ff_1_qn, and_10_out);
  or or_5 (or_5_out, d_ff_6_q, or_10_out[0]);
  Button button_6 (.out(or_8_out[2]));
  Button button_7 (.out(button_7_out));
  Register #(.width(1)) register_7 (.D(dipswitch_1_p4), .en(1'b1), .clk(clock_1_out), .Q(register_7_q), .clr(1'b0));
  xnor xnor_3 (xnor_3_out, register_6_q, register_5_q);
  Register #(.width(1)) register_8 (.D(dipswitch_2_p4), .en(1'b1), .clk(clock_2_out), .Q(register_8_q), .clr(1'b0));
  Button button_8 ();  // open: out
  D_Flip_Flop d_ff_8 (.D(1'b1), .clk(and_8_out), .Q(d_ff_8_q), .Qn(d_ff_8_qn), .reset(or_5_out));  // open: preset
  Button button_9 (.out(button_9_out));
  Button button_10 (.out(button_10_out));
  and and_9 (and_9_out, xnor_3_out, and_6_out);
  xnor xnor_4 (xnor_4_out, counter_3_q[0], counter_4_q[0]);
  or or_6 (or_6_out, button_9_out, button_10_out, button_7_out, or_8_out[2]);
  and and_10 (and_10_out, d_ff_7_q, or_6_out);
  D_Flip_Flop #(.trigger("falling")) d_ff_9 (
    .D(d_ff_8_q), .clk(and_8_out), .Q(d_ff_9_q), .reset(or_5_out));  // open: Qn, preset
  and and_11 (and_11_out, d_ff_8_q, d_ff_10_q);
  and and_12 (and_12_out, d_ff_1_qn, d_ff_11_q);
  LED led_1 (.in(and_12_out));
  xnor xnor_5 (xnor_5_out, counter_3_q[1], counter_4_q[1]);
  Hex_Digit_Display hex_digit_display_1 (.value({1'b0, counter_3_q}));  // open: dp
  xnor xnor_6 (xnor_6_out, register_7_q, register_8_q);
  or or_7 (or_7_out, and_7_out, button_11_out);
  D_Flip_Flop d_ff_10 (.D(1'b1), .clk(multiplexer_1_out), .Q(d_ff_10_q), .reset(or_5_out));  // open: Qn, preset
  not not_3 (not_3_out, d_ff_10_q);
  and and_13 (and_13_out, d_ff_8_q, not_3_out);
  and and_14 (and_14_out, d_ff_11_q, d_ff_1_q);
  LED led_2 (.in(and_14_out));
  LED led_3 (.in(and_19_out));
  and and_15 (and_15_out, xnor_6_out, and_9_out);
  xnor xnor_7 (xnor_7_out, counter_3_q[2], counter_4_q[2]);
  or or_8 (or_8_out[0], button_9_out, button_7_out);
  or or_9 (or_8_out[1], button_10_out, button_7_out);
  LED led_4 (.in(and_13_out));
  and and_16 (and_16_out, and_2_out, multiplexer_7_out);
  LED led_5 (.in(and_16_out));
  LED led_6 (.in(and_18_out));
  LED led_7 (.in(and_15_out));
  LED led_8 (.in(and_17_out));
  D_Flip_Flop d_ff_11 (.D(1'b1), .clk(button_11_out), .Q(d_ff_11_q), .reset(or_10_out[0]));  // open: Qn, preset
  Button button_11 (.out(button_11_out));
  and and_17 (and_17_out, and_2_out, multiplexer_8_out);
  Button button_12 (.out(button_12_out));
  Register #(.width(3)) register_9 (.D(or_8_out), .en(d_ff_8_qn), .clk(and_10_out), .Q(register_9_q), .clr(or_5_out));
  and and_18 (and_18_out, and_2_out, multiplexer_9_out);
  or or_10 (or_10_out[0], button_12_out, demultiplexer_6_out5);
  and and_19 (and_19_out, and_2_out, multiplexer_10_out);
  Multiplexer #(.select(3)) multiplexer_1 (
    .in0(multiplexer_2_out), .in1(multiplexer_3_out), .in2(multiplexer_4_out), .in3(multiplexer_5_out),
    .in4(multiplexer_6_out), .in5(1'b0), .in6(1'b0), .in7(1'b0), .out(multiplexer_1_out), .sel(counter_4_q));
  or or_11 (or_11_out, multiplexer_10_out, multiplexer_9_out, multiplexer_8_out, multiplexer_7_out);
  Multiplexer #(.select(3)) multiplexer_2 (
    .in0(1'b0), .in1(n74175_1_pin7), .in2(n74175_1_pin2), .in3(n74175_1_pin15), .in4(n74175_1_pin10),
    .out(multiplexer_2_out), .sel(register_9_q));  // open: in5, in6, in7
  Multiplexer #(.select(3)) multiplexer_3 (
    .in0(1'b0), .in1(n74175_2_pin7), .in2(n74175_2_pin2), .in3(n74175_2_pin15), .in4(n74175_2_pin10),
    .out(multiplexer_3_out), .sel(register_9_q));  // open: in5, in6, in7
  Multiplexer #(.select(3)) multiplexer_4 (
    .in0(1'b0), .in1(n74175_3_pin7), .in2(n74175_3_pin2), .in3(n74175_3_pin15), .in4(n74175_3_pin10),
    .out(multiplexer_4_out), .sel(register_9_q));  // open: in5, in6, in7
  Multiplexer #(.select(3)) multiplexer_5 (
    .in0(1'b0), .in1(n74175_4_pin7), .in2(n74175_4_pin2), .in3(n74175_4_pin15), .in4(n74175_4_pin10),
    .out(multiplexer_5_out), .sel(register_9_q));  // open: in5, in6, in7
  Multiplexer #(.select(3)) multiplexer_6 (
    .in0(1'b0), .in1(n74175_5_pin7), .in2(n74175_5_pin2), .in3(n74175_5_pin15), .in4(n74175_5_pin10),
    .out(multiplexer_6_out), .sel(register_9_q));  // open: in5, in6, in7
  nor nor_1 (nor_1_out, n74175_1_pin10, n74175_1_pin15, n74175_1_pin2, n74175_1_pin7);
  _74175 u_74175_1 (
    .pin1(n74175_1_pin1), .pin2(n74175_1_pin2), .pin4(n74175_1_pin4), .pin5(n74175_1_pin5),
    .pin7(n74175_1_pin7), .pin15(n74175_1_pin15), .pin13(n74175_1_pin13), .pin12(n74175_1_pin12),
    .pin10(n74175_1_pin10), .pin9(n74175_1_pin9));  // open: pin3, pin6, pin14, pin11
  _74175 u_74175_2 (
    .pin1(n74175_1_pin1), .pin2(n74175_2_pin2), .pin4(n74175_2_pin4), .pin5(n74175_2_pin5),
    .pin7(n74175_2_pin7), .pin15(n74175_2_pin15), .pin13(n74175_2_pin13), .pin12(n74175_2_pin12),
    .pin10(n74175_2_pin10), .pin9(n74175_2_pin9));  // open: pin3, pin6, pin14, pin11
  _74175 u_74175_3 (
    .pin1(n74175_1_pin1), .pin2(n74175_3_pin2), .pin4(n74175_3_pin4), .pin5(n74175_3_pin5),
    .pin7(n74175_3_pin7), .pin15(n74175_3_pin15), .pin13(n74175_3_pin13), .pin12(n74175_3_pin12),
    .pin10(n74175_3_pin10), .pin9(n74175_3_pin9));  // open: pin3, pin6, pin14, pin11
  _74175 u_74175_4 (
    .pin1(n74175_1_pin1), .pin2(n74175_4_pin2), .pin4(n74175_4_pin4), .pin5(n74175_4_pin5),
    .pin7(n74175_4_pin7), .pin15(n74175_4_pin15), .pin13(n74175_4_pin13), .pin12(n74175_4_pin12),
    .pin10(n74175_4_pin10), .pin9(n74175_4_pin9));  // open: pin3, pin6, pin14, pin11
  _74175 u_74175_5 (
    .pin1(n74175_1_pin1), .pin2(n74175_5_pin2), .pin4(n74175_5_pin4), .pin5(n74175_5_pin5),
    .pin7(n74175_5_pin7), .pin15(n74175_5_pin15), .pin13(n74175_5_pin13), .pin12(n74175_5_pin12),
    .pin10(n74175_5_pin10), .pin9(n74175_5_pin9));  // open: pin3, pin6, pin14, pin11
  and and_20 (n74175_1_pin9, nor_1_out, button_11_out);
  not not_4 (n74175_1_pin1, or_10_out[0]);
  Demultiplexer #(.select(2)) demultiplexer_1 (
    .out0(n74175_1_pin13), .out1(n74175_1_pin12), .out2(n74175_1_pin5), .out3(n74175_1_pin4), .in(1'b1),
    .sel(random_1_out));
  Demultiplexer #(.select(2)) demultiplexer_2 (
    .out0(n74175_2_pin13), .out1(n74175_2_pin12), .out2(n74175_2_pin5), .out3(n74175_2_pin4), .in(1'b1),
    .sel(random_1_out));
  Demultiplexer #(.select(2)) demultiplexer_3 (
    .out0(n74175_3_pin13), .out1(n74175_3_pin12), .out2(n74175_3_pin5), .out3(n74175_3_pin4), .in(1'b1),
    .sel(random_1_out));
  Demultiplexer #(.select(2)) demultiplexer_4 (
    .out0(n74175_4_pin13), .out1(n74175_4_pin12), .out2(n74175_4_pin5), .out3(n74175_4_pin4), .in(1'b1),
    .sel(random_1_out));
  Demultiplexer #(.select(2)) demultiplexer_5 (
    .out0(n74175_5_pin13), .out1(n74175_5_pin12), .out2(n74175_5_pin5), .out3(n74175_5_pin4), .in(1'b1),
    .sel(random_1_out));
  Multiplexer #(.select(3)) multiplexer_7 (
    .in0(n74175_1_pin7), .in1(n74175_2_pin7), .in2(n74175_3_pin7), .in3(n74175_4_pin7), .in4(n74175_5_pin7),
    .in5(1'b0), .in6(1'b0), .in7(1'b0), .out(multiplexer_7_out), .sel(counter_1_q));
  Multiplexer #(.select(3)) multiplexer_8 (
    .in0(n74175_1_pin2), .in1(n74175_2_pin2), .in2(n74175_3_pin2), .in3(n74175_4_pin2), .in4(n74175_5_pin2),
    .in5(1'b0), .in6(1'b0), .in7(1'b0), .out(multiplexer_8_out), .sel(counter_1_q));
  Multiplexer #(.select(3)) multiplexer_9 (
    .in0(n74175_1_pin15), .in1(n74175_2_pin15), .in2(n74175_3_pin15), .in3(n74175_4_pin15),
    .in4(n74175_5_pin15), .in5(1'b0), .in6(1'b0), .in7(1'b0), .out(multiplexer_9_out), .sel(counter_1_q));
  Multiplexer #(.select(3)) multiplexer_10 (
    .in0(n74175_1_pin10), .in1(n74175_2_pin10), .in2(n74175_3_pin10), .in3(n74175_4_pin10),
    .in4(n74175_5_pin10), .in5(1'b0), .in6(1'b0), .in7(1'b0), .out(multiplexer_10_out), .sel(counter_1_q));
  Demultiplexer #(.select(3)) demultiplexer_6 (
    .out0(demultiplexer_6_out0), .out1(n74175_2_pin9), .out2(n74175_3_pin9), .out3(n74175_4_pin9),
    .out4(n74175_5_pin9), .out5(demultiplexer_6_out5), .in(and_4_out), .sel(counter_3_q));  // open: out6, out7
  or or_12 (or_12_out, n74175_5_pin9, n74175_4_pin9, n74175_3_pin9, n74175_2_pin9);
  Clock clock_4 (.out(clock_4_out));
  Random #(.width(2)) random_1 (.next(1'b1), .clk(clock_4_out), .out(random_1_out));  // open: clr
  // also tied to GND on the sheet: demultiplexer_6_out0

  // Notes on the sheet:
  //   some delay before show 
  //   show until there is no data yet
  //   show all button that you must press
  //   this is counter (ic)
  //   User
  //   compare if current state hit max
  //   will go next state if release button
  //   Simon
  //   Max count
  //   current state
  //   correct
  //   it wil count first pressed
  //   prevent some kids press all button,
  //   Dont Forget to TURN ON Clock
  //   Nah
  //   still do nothing if you press wrong button
  //   give me idea plz faii, im depressed
  //   Start Game
  //   Reset Data
  //   Reset
  //   Memory 4bits * 8 => 32 bits
  //   Random
endmodule

module buttons (
  input  in_1,
  input  in_2,
  input  in_3,
  input  in_4,
  input  in_5,
  input  in_6,
  input  Data_from_memory,
  input  reset,
  output out_9,
  output [2:0] out_10,
  output out_11,
  output out_12
);

  wire and_1_out, and_2_out, d_ff_1_q, d_ff_1_qn, d_ff_2_q, d_ff_3_q, not_1_out, or_1_out, or_2_out;
  wire [1:0] or_3_out;

  Button button_1 ();  // open: out
  Button button_2 ();  // open: out
  Button button_3 ();  // open: out
  Button button_4 ();  // open: out
  and and_1 (and_1_out, in_6, and_2_out);
  or or_1 (or_1_out, out_9, reset);
  D_Flip_Flop d_ff_1 (.D(1'b1), .clk(and_1_out), .Q(d_ff_1_q), .Qn(d_ff_1_qn), .reset(or_1_out));  // open: preset
  or or_2 (or_2_out, in_1, in_3, in_2, in_4);
  and and_2 (and_2_out, in_5, or_2_out);
  D_Flip_Flop #(.trigger("falling")) d_ff_2 (
    .D(d_ff_1_q), .clk(and_1_out), .Q(d_ff_2_q), .reset(or_1_out));  // open: Qn, preset
  and and_3 (out_9, d_ff_2_q, d_ff_3_q);
  D_Flip_Flop d_ff_3 (.D(1'b1), .clk(Data_from_memory), .Q(d_ff_3_q), .reset(or_1_out));  // open: Qn, preset
  or or_3 (or_3_out[0], in_1, in_2);
  or or_4 (or_3_out[1], in_3, in_2);
  not not_1 (not_1_out, d_ff_3_q);
  and and_4 (out_12, d_ff_2_q, not_1_out);
  Register #(.width(3)) register_1 (.D({in_4, or_3_out}), .en(d_ff_1_qn), .clk(and_2_out), .Q(out_10), .clr(or_1_out));

  assign out_11 = out_9;

  // Notes on the sheet:
  //   start game
  //   not user turn (light krapib)
  //   will go next state if release button
  //   it wil count first pressed
  //   prevent some kids press all button,
  //   correct
  //   No
endmodule

module combi (
);

  wire and_1_out, and_2_out, b, b_4, buttons_1_out_9, buttons_1_out_11, buttons_1_out_12, clock_1_out,
       clock_2_out, counters_1_out_6, counters_1_out_8, d_ff_1_q, data_1_out_9, data_1_out_10, data_1_out_11,
       data_1_out_12, data_1_out_13, data_1_out_14, data_1_out_15, g, g_3, k, or_1_out, r, r_2, reset_clk,
       start_clk, u, y, y_1;
  wire [2:0] buttons_1_out_10, counters_1_out_7, counters_1_out_9, lightkrapib_1_out_15;
  wire [3:0] Seg_7;

  LED led_1 (.in(y_1));
  Button button_1 (.out(y));
  Button button_2 (.out(b));
  LED led_2 (.in(b_4));
  and and_1 (and_1_out, u, d_ff_1_q);
  LED led_3 (.in(and_1_out));
  Hex_Digit_Display hex_digit_display_1 (.value(Seg_7));  // open: dp
  and and_2 (and_2_out, d_ff_1_q, k);
  LED led_4 (.in(and_2_out));
  LED led_5 (.in(r_2));
  Button button_3 (.out(r));
  Button button_4 (.out(g));
  LED led_6 (.in(g_3));
  Button button_5 (.out(start_clk));
  Button button_6 (.out(reset_clk));
  D_Flip_Flop d_ff_1 (.D(1'b1), .clk(start_clk), .Q(d_ff_1_q), .reset(or_1_out));  // open: Qn, preset
  or or_1 (or_1_out, reset_clk, buttons_1_out_12, data_1_out_15);
  Counters counters_1 (
    .start_next_level(data_1_out_10), .in_2(reset_clk), .start(d_ff_1_q), .correct(buttons_1_out_9),
    .out_5(Seg_7), .out_6(counters_1_out_6), .out_7(counters_1_out_7), .out_9(counters_1_out_9),
    .out_8(counters_1_out_8));
  buttons buttons_1 (
    .Data_from_memory(data_1_out_9), .in_5(d_ff_1_q), .in_6(u), .in_1(y), .in_2(g), .in_3(r), .in_4(b),
    .reset(reset_clk), .out_12(buttons_1_out_12), .out_10(buttons_1_out_10), .out_9(buttons_1_out_9),
    .out_11(buttons_1_out_11));
  Clock clock_1 (.out(clock_1_out));
  Data data_1 (
    .in_1(d_ff_1_q), .Light_Krapib(lightkrapib_1_out_15), .in_2(reset_clk), .Clk_to_random(counters_1_out_6),
    .in_4(counters_1_out_7), .Clock(clock_2_out), .in_7(counters_1_out_9), .in_6(buttons_1_out_10),
    .out_11(data_1_out_11), .out_12(data_1_out_12), .out_13(data_1_out_13), .out_14(data_1_out_14),
    .out_15(data_1_out_15), .out_10(data_1_out_10), .out_9(data_1_out_9));
  LightKrapib lightkrapib_1 (
    ._1(data_1_out_11), ._2(data_1_out_12), ._3(data_1_out_13), ._4(data_1_out_14), .in_4(start_clk),
    .in_5(counters_1_out_8), .Clock(clock_1_out), .Reset(reset_clk), .out_15(lightkrapib_1_out_15),
    ._3_2(g_3), ._4_2(b_4), ._1_2(y_1), ._2_2(r_2), .out_9(k), .out_10(u));
  Clock clock_2 (.out(clock_2_out));

  // Notes on the sheet:
  //   start
  //   reset
endmodule

module Counters (
  input  start_next_level,
  input  in_2,
  input  start,
  input  correct,
  output [3:0] out_5,
  output out_6,
  output [2:0] out_7,
  output out_8,
  output [2:0] out_9
);

  wire and_2_out, not_1_out, or_1_out, or_2_out, xnor_1_out, xnor_2_out, xnor_3_out;

  and and_1 (out_6, start, and_2_out);
  or or_1 (or_1_out, out_6, in_2);
  or or_2 (or_2_out, in_2, start_next_level);
  Counter #(.max('h7), .width(3)) counter_1 (
    .load(not_1_out), .up(1'b1), .count(1'b1), .clk(or_2_out), .D(3'b001), .Q(out_5[2:0]));  // open: clr, carry
  not not_1 (not_1_out, start);
  and and_2 (and_2_out, xnor_1_out, xnor_2_out, xnor_3_out);
  Counter #(.max('h7), .width(3)) counter_2 (
    .clr(or_1_out), .up(1'b1), .count(1'b1), .clk(correct), .Q(out_9));  // open: load, D, carry
  xnor xnor_1 (xnor_1_out, out_5[0], out_9[0]);
  xnor xnor_2 (xnor_2_out, out_5[1], out_9[1]);
  xnor xnor_3 (xnor_3_out, out_5[2], out_9[2]);

  assign out_5[3] = 1'b0;
  assign out_7 = out_5[2:0];
  assign out_8 = out_6;

  // Notes on the sheet:
  //   reset
  //   start light krapib
  //   Max count
  //   compare if current state hit max
  //   current state
  //   curret level to 7 segments
  //   send clk to random next level
  //   which level must be randomed
  //   current user's state
endmodule

module Data (
  input  in_1,
  input  in_2,
  input  Clk_to_random,
  input  [2:0] in_4,
  input  Clock,
  input  [2:0] in_6,
  input  [2:0] in_7,
  input  [2:0] Light_Krapib,
  output out_9,
  output out_10,
  output out_11,
  output out_12,
  output out_13,
  output out_14,
  output out_15
);

  wire demultiplexer_6_out0, multiplexer_2_out, multiplexer_3_out, multiplexer_4_out, multiplexer_5_out,
       multiplexer_6_out, n74175_1_pin1, n74175_1_pin2, n74175_1_pin4, n74175_1_pin5, n74175_1_pin7,
       n74175_1_pin9, n74175_1_pin10, n74175_1_pin12, n74175_1_pin13, n74175_1_pin15, n74175_2_pin2,
       n74175_2_pin4, n74175_2_pin5, n74175_2_pin7, n74175_2_pin9, n74175_2_pin10, n74175_2_pin12,
       n74175_2_pin13, n74175_2_pin15, n74175_3_pin2, n74175_3_pin4, n74175_3_pin5, n74175_3_pin7,
       n74175_3_pin9, n74175_3_pin10, n74175_3_pin12, n74175_3_pin13, n74175_3_pin15, n74175_4_pin2,
       n74175_4_pin4, n74175_4_pin5, n74175_4_pin7, n74175_4_pin9, n74175_4_pin10, n74175_4_pin12,
       n74175_4_pin13, n74175_4_pin15, n74175_5_pin2, n74175_5_pin4, n74175_5_pin5, n74175_5_pin7,
       n74175_5_pin9, n74175_5_pin10, n74175_5_pin12, n74175_5_pin13, n74175_5_pin15, nor_1_out;
  wire [1:0] counter_1_q;

  Multiplexer #(.select(3)) multiplexer_1 (
    .in0(multiplexer_2_out), .in1(multiplexer_3_out), .in2(multiplexer_4_out), .in3(multiplexer_5_out),
    .in4(multiplexer_6_out), .in5(1'b0), .in6(1'b0), .in7(1'b0), .out(out_9), .sel(in_7));
  Multiplexer #(.select(3)) multiplexer_2 (
    .in0(1'b0), .in1(n74175_1_pin7), .in2(n74175_1_pin2), .in3(n74175_1_pin15), .in4(n74175_1_pin10),
    .out(multiplexer_2_out), .sel(in_6));  // open: in5, in6, in7
  Multiplexer #(.select(3)) multiplexer_3 (
    .in0(1'b0), .in1(n74175_2_pin7), .in2(n74175_2_pin2), .in3(n74175_2_pin15), .in4(n74175_2_pin10),
    .out(multiplexer_3_out), .sel(in_6));  // open: in5, in6, in7
  Multiplexer #(.select(3)) multiplexer_4 (
    .in0(1'b0), .in1(n74175_3_pin7), .in2(n74175_3_pin2), .in3(n74175_3_pin15), .in4(n74175_3_pin10),
    .out(multiplexer_4_out), .sel(in_6));  // open: in5, in6, in7
  Multiplexer #(.select(3)) multiplexer_5 (
    .in0(1'b0), .in1(n74175_4_pin7), .in2(n74175_4_pin2), .in3(n74175_4_pin15), .in4(n74175_4_pin10),
    .out(multiplexer_5_out), .sel(in_6));  // open: in5, in6, in7
  Multiplexer #(.select(3)) multiplexer_6 (
    .in0(1'b0), .in1(n74175_5_pin7), .in2(n74175_5_pin2), .in3(n74175_5_pin15), .in4(n74175_5_pin10),
    .out(multiplexer_6_out), .sel(in_6));  // open: in5, in6, in7
  nor nor_1 (nor_1_out, n74175_1_pin10, n74175_1_pin15, n74175_1_pin2, n74175_1_pin7);
  _74175 u_74175_1 (
    .pin1(n74175_1_pin1), .pin2(n74175_1_pin2), .pin4(n74175_1_pin4), .pin5(n74175_1_pin5),
    .pin7(n74175_1_pin7), .pin15(n74175_1_pin15), .pin13(n74175_1_pin13), .pin12(n74175_1_pin12),
    .pin10(n74175_1_pin10), .pin9(n74175_1_pin9));  // open: pin3, pin6, pin14, pin11
  _74175 u_74175_2 (
    .pin1(n74175_1_pin1), .pin2(n74175_2_pin2), .pin4(n74175_2_pin4), .pin5(n74175_2_pin5),
    .pin7(n74175_2_pin7), .pin15(n74175_2_pin15), .pin13(n74175_2_pin13), .pin12(n74175_2_pin12),
    .pin10(n74175_2_pin10), .pin9(n74175_2_pin9));  // open: pin3, pin6, pin14, pin11
  _74175 u_74175_3 (
    .pin1(n74175_1_pin1), .pin2(n74175_3_pin2), .pin4(n74175_3_pin4), .pin5(n74175_3_pin5),
    .pin7(n74175_3_pin7), .pin15(n74175_3_pin15), .pin13(n74175_3_pin13), .pin12(n74175_3_pin12),
    .pin10(n74175_3_pin10), .pin9(n74175_3_pin9));  // open: pin3, pin6, pin14, pin11
  _74175 u_74175_4 (
    .pin1(n74175_1_pin1), .pin2(n74175_4_pin2), .pin4(n74175_4_pin4), .pin5(n74175_4_pin5),
    .pin7(n74175_4_pin7), .pin15(n74175_4_pin15), .pin13(n74175_4_pin13), .pin12(n74175_4_pin12),
    .pin10(n74175_4_pin10), .pin9(n74175_4_pin9));  // open: pin3, pin6, pin14, pin11
  _74175 u_74175_5 (
    .pin1(n74175_1_pin1), .pin2(n74175_5_pin2), .pin4(n74175_5_pin4), .pin5(n74175_5_pin5),
    .pin7(n74175_5_pin7), .pin15(n74175_5_pin15), .pin13(n74175_5_pin13), .pin12(n74175_5_pin12),
    .pin10(n74175_5_pin10), .pin9(n74175_5_pin9));  // open: pin3, pin6, pin14, pin11
  and and_1 (n74175_1_pin9, nor_1_out, in_1);
  not not_1 (n74175_1_pin1, in_2);
  Demultiplexer #(.select(2)) demultiplexer_1 (
    .out0(n74175_1_pin13), .out1(n74175_1_pin12), .out2(n74175_1_pin5), .out3(n74175_1_pin4), .in(1'b1),
    .sel(counter_1_q));
  Demultiplexer #(.select(2)) demultiplexer_2 (
    .out0(n74175_2_pin13), .out1(n74175_2_pin12), .out2(n74175_2_pin5), .out3(n74175_2_pin4), .in(1'b1),
    .sel(counter_1_q));
  Demultiplexer #(.select(2)) demultiplexer_3 (
    .out0(n74175_3_pin13), .out1(n74175_3_pin12), .out2(n74175_3_pin5), .out3(n74175_3_pin4), .in(1'b1),
    .sel(counter_1_q));
  Demultiplexer #(.select(2)) demultiplexer_4 (
    .out0(n74175_4_pin13), .out1(n74175_4_pin12), .out2(n74175_4_pin5), .out3(n74175_4_pin4), .in(1'b1),
    .sel(counter_1_q));
  Demultiplexer #(.select(2)) demultiplexer_5 (
    .out0(n74175_5_pin13), .out1(n74175_5_pin12), .out2(n74175_5_pin5), .out3(n74175_5_pin4), .in(1'b1),
    .sel(counter_1_q));
  Multiplexer #(.select(3)) multiplexer_7 (
    .in0(n74175_1_pin7), .in1(n74175_2_pin7), .in2(n74175_3_pin7), .in3(n74175_4_pin7), .in4(n74175_5_pin7),
    .in5(1'b0), .in6(1'b0), .in7(1'b0), .out(out_11), .sel(Light_Krapib));
  Multiplexer #(.select(3)) multiplexer_8 (
    .in0(n74175_1_pin2), .in1(n74175_2_pin2), .in2(n74175_3_pin2), .in3(n74175_4_pin2), .in4(n74175_5_pin2),
    .in5(1'b0), .in6(1'b0), .in7(1'b0), .out(out_12), .sel(Light_Krapib));
  Multiplexer #(.select(3)) multiplexer_9 (
    .in0(n74175_1_pin15), .in1(n74175_2_pin15), .in2(n74175_3_pin15), .in3(n74175_4_pin15),
    .in4(n74175_5_pin15), .in5(1'b0), .in6(1'b0), .in7(1'b0), .out(out_13), .sel(Light_Krapib));
  Multiplexer #(.select(3)) multiplexer_10 (
    .in0(n74175_1_pin10), .in1(n74175_2_pin10), .in2(n74175_3_pin10), .in3(n74175_4_pin10),
    .in4(n74175_5_pin10), .in5(1'b0), .in6(1'b0), .in7(1'b0), .out(out_14), .sel(Light_Krapib));
  Demultiplexer #(.select(3)) demultiplexer_6 (
    .out0(demultiplexer_6_out0), .out1(n74175_2_pin9), .out2(n74175_3_pin9), .out3(n74175_4_pin9),
    .out4(n74175_5_pin9), .out5(out_15), .in(Clk_to_random), .sel(in_4));  // open: out6, out7
  or or_1 (out_10, n74175_5_pin9, n74175_4_pin9, n74175_3_pin9, n74175_2_pin9);
  Counter #(.max('h3), .width(2)) counter_1 (
    .load(1'b0), .up(1'b1), .count(1'b1), .clk(Clock), .Q(counter_1_q));  // open: clr, D, carry

  // Notes on the sheet:
  //   Which button is clked by
  //   Send Ans
  //   Current state that user must clk
  //   Start
  //   Reset
  //   1
  //   Memory 4bits * 8 => 32 bits
  //   2
  //   3
  //   Current Max
  //   4
  //   Go next state
  //   Played All Lvl , Reset the Game
  //   Random
endmodule

module LightKrapib (
  input  _1,
  input  _2,
  input  _3,
  input  in_4,
  input  in_5,
  input  _4,
  input  Clock,
  input  Reset,
  output out_9,
  output out_10,
  output _1_2,
  output _2_2,
  output _3_2,
  output _4_2,
  output [2:0] out_15
);

  wire and_1_out, d_ff_2_q, d_ff_2_qn, d_ff_3_q, not_1_out, or_1_out, or_2_out, or_3_out;

  or or_1 (or_1_out, in_4, in_5);
  D_Flip_Flop d_ff_1 (.D(1'b1), .clk(or_1_out), .Q(out_9), .Qn(out_10), .reset(or_2_out));  // open: preset
  D_Flip_Flop #(.trigger("falling")) d_ff_2 (
    .D(out_9), .clk(Clock), .Q(d_ff_2_q), .Qn(d_ff_2_qn), .reset(or_2_out));  // open: preset
  D_Flip_Flop #(.trigger("falling")) d_ff_3 (
    .D(d_ff_2_q), .clk(Clock), .Q(d_ff_3_q), .reset(or_2_out));  // open: Qn, preset
  or or_2 (or_2_out, and_1_out, Reset);
  not not_1 (not_1_out, or_3_out);
  and and_1 (and_1_out, d_ff_3_q, not_1_out);
  or or_3 (or_3_out, _1, _2, _3, _4);
  Counter #(.max('h7), .width(3)) counter_1 (
    .load(d_ff_2_qn), .up(1'b1), .count(1'b1), .clk(Clock), .D(3'b111), .Q(out_15));  // open: clr, carry
  and and_2 (_1_2, _1, Clock);
  and and_3 (_2_2, _2, Clock);
  and and_4 (_3_2, _3, Clock);
  and and_5 (_4_2, _4, Clock);

  // Notes on the sheet:
  //   Start Game
  //   Start From Counter
  //   krapibing
  //   not krapibing
  //   Light Krapib state
  //   Get Data for krapib
  //   Data
  //   Bury the light
endmodule
